// Logisim project p1_logic.circ as structural Verilog
module main (
  input  a,
  input  b,
  input  c,
  input  d,
  output out1,
  output out2
);

  logic_test logic_test_1 (.a(a), .b(b), .c(c), .d(d), .out1(out1), .out2(out2));

  // Notes on the sheet:
  //   Problem 1: out1 = a and b and c and d, out2 = a or b or c or d
endmodule

// VHDL entity logic_test, as the project stores it:
-- Problem 1: 4-input AND / OR
library ieee;
use ieee.std_logic_1164.all;

entity logic_test is
  port (
    a, b, c, d : in  std_logic;
    out1       : out std_logic;
    out2       : out std_logic
  );
end logic_test;

architecture bhv of logic_test is
begin
  out1 <= a and b and c and d;
  out2 <= a or b or c or d;
end bhv;
