// Logisim project p3_led_letter.circ as structural Verilog
module main (
  input  en,
  input  [2:0] dat
);

  wire a, b, c, d, dp, e, f, g;

  led_letter led_letter_1 (.en(en), .dat(dat), .display({a, b, c, d, e, f, g, dp}));
  _7_Segment_Display u_7_segment_display_1 (.g(g), .f(f), .a(a), .b(b), .e(e), .d(d), .c(c), .dp(dp));

  // Notes on the sheet:
  //   Problem 3: letters on a 7-segment display (dat 000~101 = A b C d F g)
endmodule

// VHDL entity led_letter, as the project stores it:
-- Problem 3: show letters A, b, C, d, F, g on a 7-segment display
-- display(7 downto 0) = a b c d e f g dp
library ieee;
use ieee.std_logic_1164.all;

entity led_letter is
  port (
    en      : in  std_logic;
    dat     : in  std_logic_vector(2 downto 0);
    display : out std_logic_vector(7 downto 0)
  );
end led_letter;

architecture bhv of led_letter is
begin
  process (en, dat)
  begin
    if en = '0' then
      display <= "ZZZZZZZZ";
    else
      case dat is
        when "000"  => display <= "11101110";  -- A
        when "001"  => display <= "00111110";  -- b
        when "010"  => display <= "10011100";  -- C
        when "011"  => display <= "01111010";  -- d
        when "100"  => display <= "10001110";  -- F
        when "101"  => display <= "11110110";  -- g
        when others => display <= "00000000";
      end case;
    end if;
  end process;
end bhv;
