// Logisim project p4_vote25.circ as structural Verilog
module main (
  output result
);

  wire [24:0] dipswitch_1_sw1;

  DipSwitch #(.number(25)) dipswitch_1 (
    .sw1(dipswitch_1_sw1[0]), .sw2(dipswitch_1_sw1[1]), .sw3(dipswitch_1_sw1[2]), .sw4(dipswitch_1_sw1[3]),
    .sw5(dipswitch_1_sw1[4]), .sw6(dipswitch_1_sw1[5]), .sw7(dipswitch_1_sw1[6]), .sw8(dipswitch_1_sw1[7]),
    .sw9(dipswitch_1_sw1[8]), .sw10(dipswitch_1_sw1[9]), .sw11(dipswitch_1_sw1[10]),
    .sw12(dipswitch_1_sw1[11]), .sw13(dipswitch_1_sw1[12]), .sw14(dipswitch_1_sw1[13]),
    .sw15(dipswitch_1_sw1[14]), .sw16(dipswitch_1_sw1[15]), .sw17(dipswitch_1_sw1[16]),
    .sw18(dipswitch_1_sw1[17]), .sw19(dipswitch_1_sw1[18]), .sw20(dipswitch_1_sw1[19]),
    .sw21(dipswitch_1_sw1[20]), .sw22(dipswitch_1_sw1[21]), .sw23(dipswitch_1_sw1[22]),
    .sw24(dipswitch_1_sw1[23]), .sw25(dipswitch_1_sw1[24]));
  vote25 vote25_1 (.vt(dipswitch_1_sw1), .result(result));

  // Notes on the sheet:
  //   Problem 4: 25-person voting machine (result = 1 when 13 or more vote 1)
endmodule

// VHDL entity vote25, as the project stores it:
-- Problem 4: 25-person voting machine
-- result = '1' when 13 or more of the 25 inputs are '1'
library ieee;
use ieee.std_logic_1164.all;

entity vote25 is
  port (
    vt     : in  std_logic_vector(25 downto 1);
    result : out std_logic
  );
end vote25;

architecture bhv of vote25 is
begin
  process (vt)
    variable sum : integer range 0 to 25;
  begin
    sum := 0;
    for i in 1 to 25 loop
      if vt(i) = '1' then
        sum := sum + 1;
      end if;
    end loop;

    if sum >= 13 then
      result <= '1';
    else
      result <= '0';
    end if;
  end process;
end bhv;
